# Fritzing sketch 0.Base (saved by Fritzing 0.9.3b)
breadboards: 2

parts:
  NodeMCU_v1 = NodeMCU v3 LoLin [part_number=ESP8266]

nets:
  N1: NodeMCU_v1.GND#6, NodeMCU_v1.GND#13, NodeMCU_v1.GND#16, NodeMCU_v1.GND#33

notes:
  5V
  3V

custom parts:
  NodeMCU v3 LoLin: NodeMCU v3 LoLin NodeMCU (http://www.nodemcu.com/) is an open source IoT platform. It includes firmware (https://nodemcu-build.com/) which runs on the ESP8266 Wi-Fi SoC from Espressif Systems, and hardware which is based on the ESP-12E module. The term "NodeMCU" by default refers to the firmware rather than the dev kits. The firmware uses the Lua scripting language. It is based on the eLua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
