# Fritzing sketch 2.DHT-LCD (saved by Fritzing 0.9.3b)
breadboards: 2

parts:
  NodeMCU_v1 = NodeMCU v3 LoLin [part_number=ESP8266]
  Part1 = KY-015 Temperature & Humidity Sensor Module [package="Breakout board"]
  Componente1 = LCD1602-I2C

nets:
  N1: NodeMCU_v1.D3, Componente1.SDA
  N2: NodeMCU_v1.D4, Componente1.SCL
  N3: NodeMCU_v1.GND#6, NodeMCU_v1.GND#13, NodeMCU_v1.GND#16, NodeMCU_v1.GND#33, Part1.-, Componente1.GND
  N4: NodeMCU_v1.D5, Part1.S
  VIN: NodeMCU_v1.VU, Part1.Vin, Componente1.VCC

notes:
  5V
  3V

custom parts:
  NodeMCU v3 LoLin: NodeMCU v3 LoLin NodeMCU (http://www.nodemcu.com/) is an open source IoT platform. It includes firmware (https://nodemcu-build.com/) which runs on the ESP8266 Wi-Fi SoC from Espressif Systems, and hardware which is based on the ESP-12E module. The term "NodeMCU" by default refers to the firmware rather than the dev kits. The firmware uses the Lua scripting language. It is based on the eLua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
  KY-015 Temperature & Humidity Sensor Module: KY-015 temperature and humidity sensor module, provides a low-latency serial interface to measure humidity and temperature.
  LCD1602-I2C: A standard character display, usually with 2x16 characters. Comes in many colors with LCM1602 IIC attached.
