# Fritzing sketch 5.DHT-LCD-wifi-HSuelo (saved by Fritzing 0.9.3b)
breadboards: 2

parts:
  NodeMCU_v1 = NodeMCU v3 LoLin [part_number=ESP8266]
  Part1 = KY-015 Temperature & Humidity Sensor Module [package="Breakout board"]
  Componente1 = LCD1602-I2C
  Componente2 = FC-28 Soil Hygrometer Module - Probe
  Componente3 = FC-28 Soil Hygrometer Module

nets:
  N1: NodeMCU_v1.D3, Componente1.SDA
  N2: NodeMCU_v1.D4, Componente1.SCL
  3V3: NodeMCU_v1.3V3, Componente3.VCC
  GND: NodeMCU_v1.GND#6, NodeMCU_v1.GND#13, NodeMCU_v1.GND#16, NodeMCU_v1.GND#33, Part1.-, Componente1.GND, Componente3.GND
  N3: NodeMCU_v1.D5, Part1.S
  VIN: NodeMCU_v1.VU, Part1.Vin, Componente1.VCC
  N4: NodeMCU_v1.A0, Componente3.AO
  N5: Componente2.POS, Componente3.POS
  N6: Componente2.NEG, Componente3.NEG

notes:
  5V
  3V

custom parts:
  NodeMCU v3 LoLin: NodeMCU v3 LoLin NodeMCU (http://www.nodemcu.com/) is an open source IoT platform. It includes firmware (https://nodemcu-build.com/) which runs on the ESP8266 Wi-Fi SoC from Espressif Systems, and hardware which is based on the ESP-12E module. The term "NodeMCU" by default refers to the firmware rather than the dev kits. The firmware uses the Lua scripting language. It is based on the eLua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
  KY-015 Temperature & Humidity Sensor Module: KY-015 temperature and humidity sensor module, provides a low-latency serial interface to measure humidity and temperature.
  LCD1602-I2C: A standard character display, usually with 2x16 characters. Comes in many colors with LCM1602 IIC attached.
  FC-28 Soil Hygrometer Module - Probe: The FC-28 is a soil hygrometer module that uses the Texas Instruments LM393 comparator chip to provide an analog measurement of soil humidity.
  FC-28 Soil Hygrometer Module: The FC-28 is a soil hygrometer module that uses the Texas Instruments LM393 comparator chip to provide an analog measurement of soil humidity. The digital output is high when soil moisture is over a certain threshold, as determined by adjusting the potentiometer.
